# Fritzing sketch Diagram (saved by Fritzing 0.9.10b)
stripboards: 2

parts:
  WeMos_D1_Mini1 = WeMos D1 Mini
  J1 = Power Jack [package=power_jack_smd]
  M1 = RioRand LM2596
  Q1 = Basic FET N-Channel [package="DPak [SMD]"]
  R1 = Resistor [tolerance=±5% resistance=10k package="0402 [SMD]"]
  Q2 = Basic FET N-Channel [package="DPak [SMD]"]
  Q3 = Basic FET N-Channel [package="DPak [SMD]"]
  R2 = Resistor [tolerance=±5% resistance=10k package="0402 [SMD]"]
  R3 = Resistor [tolerance=±5% resistance=10k package="0402 [SMD]"]
  RHT1 = Humidity and Temperature Sensor RHT03
  R4 = Resistor [tolerance=±5% resistance=220 package="0402 [SMD]"]

nets:
  5V: WeMos_D1_Mini1.5V, M1.Pin_3, RHT1.Vcc, R4.Pin_0
  N1: WeMos_D1_Mini1.D4, R4.Pin_1
  N2: WeMos_D1_Mini1.D5, Q1.Gate, R1.Pin_1
  N3: WeMos_D1_Mini1.D6, R2.Pin_1
  N4: WeMos_D1_Mini1.D7, R3.Pin_1
  N5: WeMos_D1_Mini1.G, M1.Pin_4, R1.Pin_0, R2.Pin_0, R3.Pin_0, RHT1.GND_2
  N6: J1.GND, M1.Pin_2
  N7: J1.GNDBREAK, M1.Pin_1, Q1.source, Q2.source, Q3.drain, Q3.source

notes:
  12v
  5v
